# Fritzing sketch morse code keyer tiny fritzing drawing (saved by Fritzing 0.9.3b)
breadboards: 2

parts:
  IC1 = IC, DIP package, 14 pins [chip_label=Attiny3224]
  TRS1 = Audio Jack (TRS) 3.5mm [package="4Ucon 08780 [THT]"]
  R1 = Trimmer Potentiometer [maximum_resistance=10kΩ package=THT]
  R2 = Resistor [tolerance=±5% resistance=10k package=THT]
  R3 = Resistor [tolerance=±5% resistance=10k package=THT]
  J1 = Piezo Speaker
  OLED1 = OLED 128x64 I2C Monochrome Display GND-VDD
  TP1 = TP4056 [chip_label=TP4056 package="DIP (Dual Inline) [THT]"]
  U1 = LIPO-1000mAh [package=lipo-1000]
  J2 = female pin header, 3 pins [form="♀ (female)"]
  S1 = Toggle Switch [package=THT]

nets:
  N1: IC1.pin1, R1.leg2, R2.Pin_0, R3.Pin_0, OLED1.VDD, J2.pin1, S1.COM
  N2: IC1.pin3, TRS1.Ring, R2.Pin_1
  N3: IC1.pin4, TRS1.Tip, R3.Pin_1
  N4: IC1.pin5, R1.wiper
  N5: IC1.pin8, OLED1.SDA
  N6: IC1.pin9, OLED1.SCK
  N7: IC1.pin10, J2.pin2
  N8: IC1.pin11, J1.pin2
  N9: IC1.pin14, TRS1.Sleeve, R1.leg1, J1.pin1, OLED1.GND, TP1.pin6, J2.pin3
  N10: TP1.pin3, S1.L1
  N11: TP1.pin4, U1.+
  N12: TP1.pin5, U1.-

notes:
  UPDI

custom parts:
  OLED 128x64 I2C Monochrome Display GND-VDD: OLED 128x64 I2C Monochrome Display. Note: there are two variants of this part, this one is the GND VDD SCK SDA variant. The other is VDD GND SCK SDA. Make sure you select the part that matches your module as using the incorrect part will probably destroy your module! In addition the mounting holes are marked on silkscreen but not by default drilled. If you want drilled mounting holes, copy a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
  TP4056: A DIP stand-in part for whatever IC you want. With 6 pins on a 300mil dual inline package (DIP) footprint.
